// Logisim project Panel_De_Instrumentos.circ as structural Verilog: 5 circuits, main circuit main
module main (
);

  wire clock_1_out, direccionales_1_out_2, direccionales_2_out_2, L, LIGHT, Nivel, ON, R, sensores_1_out_5,
       sensores_2_out_5, sensores_4_out_5, sensores_5_out_5, undriven, undriven_2;
  wire [3:0] unidades_1_out_2, unidades_1_out_3, unidades_1_out_4, unidades_2_out_2, unidades_2_out_3,
       unidades_2_out_4, unidades_3_out_2, unidades_3_out_3, unidades_3_out_4, unidades_4_out_2,
       unidades_4_out_3, unidades_4_out_4;
  wire [5:0] slider_3_out, slider_4_out;
  wire [7:0] AntiColisiones, C, Li, PSI, sensores_1_out_6, sensores_2_out_6, sensores_3_out_6,
       sensores_4_out_6, Velocimetro;

  Sensores sensores_1 (
    .Input(ON), .in_2(C), .in_3(8'h96), .in_4(8'h46), .out_5(sensores_1_out_5), .out_6(sensores_1_out_6));
  Hex_Digit_Display hex_digit_display_1 (.value(unidades_1_out_4));  // open: dp
  Unidades unidades_1 (
    .in_1(sensores_1_out_6), .out_2(unidades_1_out_2), .out_3(unidades_1_out_3), .out_4(unidades_1_out_4));
  Hex_Digit_Display hex_digit_display_2 (.value(unidades_1_out_3));  // open: dp
  Sensores sensores_2 (
    .Input(ON), .in_2(PSI), .in_3(8'h21), .in_4(8'h1b), .out_5(sensores_2_out_5), .out_6(sensores_2_out_6));
  Unidades unidades_2 (
    .in_1(sensores_2_out_6), .out_2(unidades_2_out_2), .out_3(unidades_2_out_3), .out_4(unidades_2_out_4));
  Hex_Digit_Display hex_digit_display_3 (.value(unidades_2_out_3), .dp(undriven));
  Hex_Digit_Display hex_digit_display_4 (.value(unidades_2_out_4));  // open: dp
  LED led_1 (.in(ON));
  LED led_2 (.in(sensores_1_out_5));
  Hex_Digit_Display hex_digit_display_5 (.value(unidades_1_out_2));  // open: dp
  LED led_3 (.in(sensores_2_out_5));
  Hex_Digit_Display hex_digit_display_6 (.value(unidades_2_out_2), .dp(undriven_2));
  LED led_4 (.in(direccionales_1_out_2));
  Direccionales direccionales_1 (.Input(L), .out_2(direccionales_1_out_2));
  Sensores sensores_3 (.Input(ON), .in_2(Velocimetro), .out_6(sensores_3_out_6));  // open: in_3, in_4, out_5
  Hex_Digit_Display hex_digit_display_7 (.value(unidades_3_out_4));  // open: dp
  Direccionales direccionales_2 (.Input(R), .out_2(direccionales_2_out_2));
  LED led_5 (.in(direccionales_2_out_2));
  Hex_Digit_Display hex_digit_display_8 (.value(unidades_3_out_2));  // open: dp
  Unidades unidades_3 (
    .in_1(sensores_3_out_6), .out_2(unidades_3_out_2), .out_3(unidades_3_out_3), .out_4(unidades_3_out_4));
  Hex_Digit_Display hex_digit_display_9 (.value(unidades_3_out_3));  // open: dp
  // RGBLed rgbled_1: pin names not known; wires that end beside it: LIGHT
  ControlDeLuz controldeluz_1 (.Input(LIGHT), .in_2(Nivel));  // open: out_3
  Hex_Digit_Display hex_digit_display_10 (.value(unidades_4_out_3));  // open: dp
  Hex_Digit_Display hex_digit_display_11 (.value(unidades_4_out_4));  // open: dp
  Sensores sensores_4 (
    .Input(ON), .in_2(Li), .in_3(8'h3f), .in_4(8'hf), .out_5(sensores_4_out_5), .out_6(sensores_4_out_6));
  Unidades unidades_4 (
    .in_1(sensores_4_out_6), .out_2(unidades_4_out_2), .out_3(unidades_4_out_3), .out_4(unidades_4_out_4));
  LED led_6 (.in(sensores_4_out_5));
  Hex_Digit_Display hex_digit_display_12 (.value(unidades_4_out_2));  // open: dp
  Sensores sensores_5 (
    .Input(ON), .in_2(AntiColisiones), .in_3({8{1'b1}}), .in_4({8{1'b0}}), .out_5(sensores_5_out_5));  // open: out_6
  LED led_7 (.in(sensores_5_out_5));
  Clock clock_1 (.out(clock_1_out));
  Slider #(.value('h8a)) slider_1 (.out(Velocimetro));
  Slider #(.value('h5c)) slider_2 (.out(C));
  Slider #(.width(6), .value('h1b)) slider_3 (.out(slider_3_out));
  Slider #(.width(6), .value('h18)) slider_4 (.out(slider_4_out));
  Random random_1 (.clk(clock_1_out), .out(AntiColisiones));  // open: next, clr
  // DipSwitch dipswitch_1: pin names not known; wires that end beside it: ON, L, R
  // Switch switch_1: pin names not known; wires that end beside it: 1'b1, LIGHT, Nivel
  // Probe on Velocimetro
  // Probe on C
  // Probe on slider_3_out
  assign Li = {{2{1'b0}}, slider_4_out};  // Bit_Extender bit_extender_1
  // Probe on slider_4_out
  assign PSI = {{2{1'b0}}, slider_3_out};  // Bit_Extender bit_extender_2

  // Notes on the sheet:
  //   Presión de neumaticos
  //   Encendido
  //   Temperatura
  //   °C
  //   PSI
  //   Panel de Instrumentos de un Vehiculo
  //   L
  //   Direccionales
  //   R
  //   Velocimetro
  //   KM/H
  //   Luz frontal
  //   Sensor de Anticolisíon
  //   Combustible
  //   L
  //   Luces y Encendido
  //   Nivel de Luz
  //   Velocimetro
  //   Temperatura
  //   Presión de neumaticos
  //   Combustible
  //   Controles Del Vehiculo
endmodule

module Unidades (
  input  [7:0] in_1,
  output [3:0] out_2,
  output [3:0] out_3,
  output [3:0] out_4
);

  wire _100, _200, and_1_out, and_2_out, and_3_out, and_4_out, and_5_out, and_6_out, and_7_out, and_8_out,
       and_9_out, comparator_1_eq, comparator_1_gt, comparator_2_eq, comparator_2_gt, comparator_2_lt,
       comparator_3_eq, comparator_3_gt, comparator_3_lt, comparator_4_eq, comparator_4_gt, comparator_5_eq,
       comparator_5_gt, comparator_6_eq, comparator_6_gt, comparator_7_eq, comparator_7_gt, comparator_8_eq,
       comparator_8_gt, comparator_9_eq, comparator_9_gt, comparator_10_eq, comparator_10_gt,
       comparator_11_eq, comparator_11_gt, not_1_out, not_2_out, not_3_out, not_4_out, not_5_out, not_6_out,
       not_7_out, not_8_out, or_1_out, or_4_out, or_5_out, or_6_out, or_7_out, or_8_out, or_9_out, or_10_out,
       or_11_out, or_12_out;
  wire [3:0] multiplexer_3_out;
  wire [7:0] bit_extender_1_out, multiplexer_1_out, multiplexer_2_out, multiplier_1_out, registro;
  wire [7:4] subtractor_2_out;

  or or_1 (or_1_out, _200, _100);
  Comparator #(.mode("unsigned")) comparator_1 (
    .a(in_1), .b(8'hc8), .gt(comparator_1_gt), .eq(comparator_1_eq));  // open: lt
  Comparator #(.mode("unsigned")) comparator_2 (
    .a(in_1), .b(8'h64), .gt(comparator_2_gt), .eq(comparator_2_eq), .lt(comparator_2_lt));
  Multiplexer #(.width(8), .enable("false")) multiplexer_1 (
    .in0(8'h64), .in1(8'hc8), .out(multiplexer_1_out), .sel(_200));
  assign bit_extender_1_out = {{4{1'b0}}, out_3};  // Bit_Extender bit_extender_1
  or or_2 (_200, comparator_1_gt, comparator_1_eq);
  or or_3 (_100, comparator_2_gt, comparator_2_eq);
  Multiplexer #(.width(8), .enable("false")) multiplexer_2 (
    .in0({8{1'b0}}), .in1(multiplexer_1_out), .out(multiplexer_2_out), .sel(or_1_out));
  Multiplier multiplier_1 (.a(bit_extender_1_out), .b(8'ha), .out(multiplier_1_out));  // open: cin, cout
  Subtractor subtractor_1 (.a(in_1), .b(multiplexer_2_out), .out(registro));  // open: bin, bout
  Subtractor subtractor_2 (.a(registro), .b(multiplier_1_out), .out({subtractor_2_out, out_2}));  // open: bin, bout
  and and_1 (and_1_out, _200, _100);
  Multiplexer #(.width(4), .enable("false")) multiplexer_3 (
    .in0(4'b0001), .in1(4'b0010), .out(multiplexer_3_out), .sel(and_1_out));
  Multiplexer #(.width(4), .enable("false")) multiplexer_4 (
    .in0(multiplexer_3_out), .in1(4'b0000), .out(out_4), .sel(comparator_2_lt));
  Comparator #(.mode("unsigned")) comparator_3 (
    .a(registro), .b(8'ha), .gt(comparator_3_gt), .eq(comparator_3_eq), .lt(comparator_3_lt));
  or or_4 (or_4_out, comparator_3_gt, comparator_3_eq);
  or or_5 (or_5_out, comparator_4_gt, comparator_4_eq);
  Comparator #(.mode("unsigned")) comparator_4 (
    .a(registro), .b(8'h14), .gt(comparator_4_gt), .eq(comparator_4_eq));  // open: lt
  Comparator #(.mode("unsigned")) comparator_5 (
    .a(registro), .b(8'h1e), .gt(comparator_5_gt), .eq(comparator_5_eq));  // open: lt
  or or_6 (or_6_out, comparator_5_gt, comparator_5_eq);
  or or_7 (or_7_out, comparator_6_gt, comparator_6_eq);
  Comparator #(.mode("unsigned")) comparator_6 (
    .a(registro), .b(8'h28), .gt(comparator_6_gt), .eq(comparator_6_eq));  // open: lt
  Comparator #(.mode("unsigned")) comparator_7 (
    .a(registro), .b(8'h32), .gt(comparator_7_gt), .eq(comparator_7_eq));  // open: lt
  or or_8 (or_8_out, comparator_7_gt, comparator_7_eq);
  Comparator #(.mode("unsigned")) comparator_8 (
    .a(registro), .b(8'h3c), .gt(comparator_8_gt), .eq(comparator_8_eq));  // open: lt
  or or_9 (or_9_out, comparator_8_gt, comparator_8_eq);
  Comparator #(.mode("unsigned")) comparator_9 (
    .a(registro), .b(8'h46), .gt(comparator_9_gt), .eq(comparator_9_eq));  // open: lt
  or or_10 (or_10_out, comparator_9_gt, comparator_9_eq);
  Comparator #(.mode("unsigned")) comparator_10 (
    .a(registro), .b(8'h50), .gt(comparator_10_gt), .eq(comparator_10_eq));  // open: lt
  or or_11 (or_11_out, comparator_10_gt, comparator_10_eq);
  Comparator #(.mode("unsigned")) comparator_11 (
    .a(registro), .b(8'h5a), .gt(comparator_11_gt), .eq(comparator_11_eq));  // open: lt
  or or_12 (or_12_out, comparator_11_gt, comparator_11_eq);
  and and_2 (and_2_out, or_4_out, not_1_out);
  not not_1 (not_1_out, or_5_out);
  and and_3 (and_3_out, or_5_out, not_2_out);
  not not_2 (not_2_out, or_6_out);
  and and_4 (and_4_out, or_6_out, not_3_out);
  not not_3 (not_3_out, or_7_out);
  and and_5 (and_5_out, or_7_out, not_4_out);
  not not_4 (not_4_out, or_8_out);
  and and_6 (and_6_out, or_8_out, not_5_out);
  not not_5 (not_5_out, or_9_out);
  and and_7 (and_7_out, or_9_out, not_6_out);
  not not_6 (not_6_out, or_10_out);
  and and_8 (and_8_out, or_10_out, not_7_out);
  not not_7 (not_7_out, or_11_out);
  and and_9 (and_9_out, or_11_out, not_8_out);
  not not_8 (not_8_out, or_12_out);
  Transistor #(.\type ("n"), .width(4)) transistor_1 (.in(4'b0000), .out(out_3), .gate(comparator_3_lt));
  Transistor #(.\type ("n"), .width(4)) transistor_2 (.in(4'b0001), .out(out_3), .gate(and_2_out));
  Transistor #(.\type ("n"), .width(4)) transistor_3 (.in(4'b0010), .out(out_3), .gate(and_3_out));
  Transistor #(.\type ("n"), .width(4)) transistor_4 (.in(4'b0011), .out(out_3), .gate(and_4_out));
  Transistor #(.\type ("n"), .width(4)) transistor_5 (.in(4'b0100), .out(out_3), .gate(and_5_out));
  Transistor #(.\type ("n"), .width(4)) transistor_6 (.in(4'b0101), .out(out_3), .gate(and_6_out));
  Transistor #(.\type ("n"), .width(4)) transistor_7 (.in(4'b0110), .out(out_3), .gate(and_7_out));
  Transistor #(.\type ("n"), .width(4)) transistor_8 (.in(4'b0111), .out(out_3), .gate(and_8_out));
  Transistor #(.\type ("n"), .width(4)) transistor_9 (.in(4'b1000), .out(out_3), .gate(and_9_out));
  Transistor #(.\type ("n"), .width(4)) transistor_10 (.in(4'b1001), .out(out_3), .gate(or_12_out));

  // Other names for the same wires on the sheet: first[3:0] = out_2; numero[7:0] = in_1; second[3:0] = out_3;
  //   third[3:0] = out_4

  // Notes on the sheet:
  //   Input
  //   output
endmodule

module Sensores (
  input  Input,
  input  [7:0] in_2,
  input  [7:0] in_3,
  input  [7:0] in_4,
  output out_5,
  output [7:0] out_6
);

  wire clock_1_out, comparator_1_eq, comparator_1_gt, comparator_2_eq, comparator_2_lt, multiplexer_2_out,
       or_1_out, or_2_out, or_3_out;

  // Probe on in_2
  Comparator #(.mode("unsigned")) comparator_1 (
    .a(out_6), .b(in_3), .gt(comparator_1_gt), .eq(comparator_1_eq));  // open: lt
  or or_1 (or_1_out, comparator_1_gt, comparator_1_eq);
  Comparator #(.mode("unsigned")) comparator_2 (
    .a(out_6), .b(in_4), .eq(comparator_2_eq), .lt(comparator_2_lt));  // open: gt
  or or_2 (or_2_out, comparator_2_eq, comparator_2_lt);
  Multiplexer #(.width(8), .enable("false")) multiplexer_1 (.in0({8{1'b0}}), .in1(in_2), .out(out_6), .sel(Input));
  Multiplexer #(.enable("false")) multiplexer_2 (.in0(1'b0), .in1(or_3_out), .out(multiplexer_2_out), .sel(Input));
  or or_3 (or_3_out, or_1_out, or_2_out);
  Clock clock_1 (.out(clock_1_out));
  Transistor #(.\type ("n")) transistor_1 (.in(clock_1_out), .out(out_5), .gate(multiplexer_2_out));

  // Other names for the same wires on the sheet: InDato[7:0] = in_2; LED = out_5; Max[7:0] = in_3; Min[7:0] = in_4;
  //   ON = Input; OutDato[7:0] = out_6

  // Notes on the sheet:
  //   Output
endmodule

module ControlDeLuz (
  input  Input,
  input  in_2,
  output out_3
);

  and and_1 (out_3, Input, in_2);

  // Other names for the same wires on the sheet: InNivel = in_2; Luz = Input; OutNivel = out_3

  // Notes on the sheet:
  //   Output
endmodule

module Direccionales (
  input  Input,
  output out_2
);

  wire clock_1_out;

  Clock clock_1 (.out(clock_1_out));
  Transistor #(.\type ("n")) transistor_1 (.in(clock_1_out), .out(out_2), .gate(Input));

  // Other names for the same wires on the sheet: Direccional = Input; Led = out_2
endmodule
