// Logisim project Panel_De_Instrumentos.circ as structural Verilog
module main (
);

  wire L, LIGHT, ON, R;
  wire [5:0] C, Li, PSI;
  wire [7:0] Velocimetro;

  Hex_Digit_Display hex_digit_display_1 ();  // open: value, dp
  Hex_Digit_Display hex_digit_display_2 ();  // open: value, dp
  LED led_1 (.in(ON));
  LED led_2 ();  // open: in
  Hex_Digit_Display hex_digit_display_3 ();  // open: value, dp
  LED led_3 ();  // open: in
  Hex_Digit_Display hex_digit_display_4 ();  // open: value, dp
  LED led_4 (.in(L));
  Hex_Digit_Display hex_digit_display_5 ();  // open: value, dp
  LED led_5 (.in(R));
  Hex_Digit_Display hex_digit_display_6 ();  // open: value, dp
  Hex_Digit_Display hex_digit_display_7 ();  // open: value, dp
  LED led_6 (.in(LIGHT));
  Hex_Digit_Display hex_digit_display_8 ();  // open: value, dp
  Hex_Digit_Display hex_digit_display_9 ();  // open: value, dp
  LED led_7 ();  // open: in
  LED led_8 ();  // open: in
  // DipSwitch dipswitch_1: pin names not known; wires that end beside it: ON, L, R, LIGHT
  Slider slider_1 (.out(Velocimetro));
  // Probe on Velocimetro
  Slider #(.width(6)) slider_2 (.out(C));
  // Probe on C
  Slider #(.width(6)) slider_3 (.out(PSI));
  // Probe on PSI
  Slider #(.width(6)) slider_4 (.out(Li));
  // Probe on Li

  // Notes on the sheet:
  //   Temperatura
  //   Encendido
  //    °C
  //   Presión de neumaticos
  //   PSI
  //   Panel de Instrumentos de un Vehiculo
  //   L
  //   Direccionales
  //   R
  //   Velocimetro
  //   KM/H
  //   Luz frontal
  //   Sensor de colisíon
  //   Combustible
  //   L
endmodule
